# Fritzing sketch ESCservo (saved by Fritzing 0.8.3b)
breadboards: 1

parts:
  Part1 = Arduino Uno (Rev3)
  Power_plug1 = Power plug
  J1 = Basic Servo
  R1 = Resistor [tolerance=±5% resistance=1k package=THT]
  Q1 = PNP-Transistor [package="TO92 [THT]"]

nets:
  GND: Part1.GND, Power_plug1.GND, J1.gnd
  N1: Part1.D6_PWM, R1.Pin_0
  N2: Part1.D7, Q1.B
  N3: Power_plug1.VCC, Q1.C
  N4: J1.vcc, Q1.E
  N5: J1.pulse, R1.Pin_1
